// Logisim project 4-by-3-memory.circ as structural Verilog: 1 circuit, main circuit main
module main (
  input  Write_Address,
  input  in_2,
  input  D_3,
  input  D_2,
  input  D_1,
  input  D_0,
  input  WE,
  input  Read_Address,
  input  in_9,
  output Q_3,
  output Q_2,
  output Q_1,
  output Q_0
);

  wire d_ff_1_q, d_ff_2_q, d_ff_3_q, d_ff_4_q, d_ff_5_q, d_ff_6_q, d_ff_7_q, d_ff_8_q, d_ff_9_q, d_ff_10_q,
       d_ff_11_q, d_ff_12_q, decoder_1_out0, decoder_1_out1, decoder_1_out2;

  Decoder #(.select(2), .enable("false")) decoder_1 (
    .out0(decoder_1_out0), .out1(decoder_1_out1), .out2(decoder_1_out2), .sel({Write_Address, in_2}));  // open: out3
  D_Flip_Flop d_ff_1 (.clk(WE), .D(D_3), .Q(d_ff_1_q), .en(decoder_1_out1));  // open: Qn, preset, reset
  D_Flip_Flop d_ff_2 (.clk(WE), .D(D_3), .Q(d_ff_2_q), .en(decoder_1_out0));  // open: Qn, preset, reset
  D_Flip_Flop d_ff_3 (.clk(WE), .D(D_3), .Q(d_ff_3_q), .en(decoder_1_out2));  // open: Qn, preset, reset
  Multiplexer #(.select(2), .enable("false")) multiplexer_1 (
    .in0(d_ff_2_q), .in1(d_ff_1_q), .in2(d_ff_3_q), .out(Q_3), .sel({Read_Address, in_9}));  // open: in3
  D_Flip_Flop d_ff_4 (.clk(WE), .D(D_2), .Q(d_ff_4_q), .en(decoder_1_out2));  // open: Qn, preset, reset
  D_Flip_Flop d_ff_5 (.clk(WE), .D(D_2), .Q(d_ff_5_q), .en(decoder_1_out1));  // open: Qn, preset, reset
  D_Flip_Flop d_ff_6 (.clk(WE), .D(D_2), .Q(d_ff_6_q), .en(decoder_1_out0));  // open: Qn, preset, reset
  Multiplexer #(.select(2), .enable("false")) multiplexer_2 (
    .in0(d_ff_6_q), .in1(d_ff_5_q), .in2(d_ff_4_q), .out(Q_2), .sel({Read_Address, in_9}));  // open: in3
  D_Flip_Flop d_ff_7 (.clk(WE), .D(D_1), .Q(d_ff_7_q), .en(decoder_1_out2));  // open: Qn, preset, reset
  D_Flip_Flop d_ff_8 (.clk(WE), .D(D_1), .Q(d_ff_8_q), .en(decoder_1_out1));  // open: Qn, preset, reset
  D_Flip_Flop d_ff_9 (.clk(WE), .D(D_1), .Q(d_ff_9_q), .en(decoder_1_out0));  // open: Qn, preset, reset
  Multiplexer #(.select(2), .enable("false")) multiplexer_3 (
    .in0(d_ff_9_q), .in1(d_ff_8_q), .in2(d_ff_7_q), .out(Q_1), .sel({Read_Address, in_9}));  // open: in3
  D_Flip_Flop d_ff_10 (.clk(WE), .D(D_0), .Q(d_ff_10_q), .en(decoder_1_out0));  // open: Qn, preset, reset
  D_Flip_Flop d_ff_11 (.clk(WE), .D(D_0), .Q(d_ff_11_q), .en(decoder_1_out2));  // open: Qn, preset, reset
  D_Flip_Flop d_ff_12 (.clk(WE), .D(D_0), .Q(d_ff_12_q), .en(decoder_1_out1));  // open: Qn, preset, reset
  Multiplexer #(.select(2), .enable("false")) multiplexer_4 (
    .in0(d_ff_10_q), .in1(d_ff_12_q), .in2(d_ff_11_q), .out(Q_0), .sel({Read_Address, in_9}));  // open: in3

  // Notes on the sheet:
  //   Address space: 3
  //   Addressability: 4-bit
  //   Nibble at address 10
  //   Nibble at address 01
  //   Nibble at address 00
endmodule
