// Logisim project ALU.circ as structural Verilog: 1 circuit, main circuit main
// op
module main (
  input  [31:0] operand_0,
  input  [3:0] operation,
  input  [31:0] operand_1,
  output [31:0] result
);
endmodule
