// Logisim project condition-code-register.circ as structural Verilog: 1 circuit, main circuit main
module main (
  input  [31:0] operand,
  input  Id_cc,
  output N,
  output Z,
  output P
);

  wire comparator_1_eq, not_1_out;

  Comparator #(.width(32)) comparator_1 (.a({32{1'b0}}), .b(operand), .eq(comparator_1_eq));  // open: gt, lt
  not not_1 (not_1_out, comparator_1_eq);
  Multiplexer multiplexer_1 (.in0(1'b1), .in1(operand[31]), .out(N), .sel(Id_cc));  // open: en
  Multiplexer multiplexer_2 (.in0(1'b1), .in1(not_1_out), .out(Z), .sel(Id_cc));  // open: en
  Multiplexer multiplexer_3 (.in0(1'b1), .in1(operand[31]), .out(P), .sel(Id_cc));  // open: en
endmodule
