// Logisim project d-flip-flop.circ as structural Verilog: 1 circuit, main circuit main
module main (
  input  D,
  input  clk,
  input  in_3,
  input  in_4,
  output Q,
  output not_Q,
  output out_7,
  output out_8
);

  wire and_1_out, nand_1_out, nand_2_out, not_1_out, not_2_out;

  not not_1 (not_1_out, clk);
  // Probe on and_1_out
  and and_1 (and_1_out, clk, not_1_out);
  not not_2 (not_2_out, D);
  // Probe on nand_1_out
  nand nand_1 (nand_1_out, D, and_1_out);
  nand nand_2 (nand_2_out, and_1_out, not_2_out);
  // Probe on nand_2_out
  D_Flip_Flop d_ff_1 (.clk(in_3), .D(in_4), .Q(out_7), .Qn(out_8));  // open: preset, en, reset
  nand nand_3 (Q, nand_1_out, not_Q);
  nand nand_4 (not_Q, Q, nand_2_out);
endmodule
