// Logisim project gated-d-latch.circ as structural Verilog: 1 circuit, main circuit main
module main (
  input  D,
  input  WE,
  output Q,
  output not_Q
);

  wire nand_1_out, nand_2_out, not_1_out;

  not not_1 (not_1_out, D);
  // Probe on nand_1_out
  nand nand_1 (nand_1_out, D, WE);
  nand nand_2 (nand_2_out, WE, not_1_out);
  // Probe on nand_2_out
  nand nand_3 (Q, nand_1_out, not_Q);
  nand nand_4 (not_Q, Q, nand_2_out);
endmodule
