// Logisim project memory-modules.circ as structural Verilog: 2 circuits, main circuit two
module two (
  input  [31:0] in_1,
  output [7:0] out_2
);

  wire [7:0] ram_1_data, ram_2_data;

  RAM #(.addrWidth(10)) ram_1 (.addr(in_1[9:0]), .data(ram_1_data));  // open: sel, clk, ld, clr
  RAM #(.addrWidth(10)) ram_2 (.addr(in_1[9:0]), .data(ram_2_data));  // open: sel, clk, ld, clr
  Multiplexer #(.width(8), .enable("false")) multiplexer_1 (
    .in0(ram_1_data), .in1(ram_2_data), .out(out_2), .sel(in_1[10]));
endmodule

module four (
  input  [31:0] in_1,
  output [7:0] out_2
);

  wire [7:0] ram_1_data, ram_2_data, ram_3_data, ram_4_data;

  RAM #(.addrWidth(10)) ram_1 (.addr(in_1[9:0]), .data(ram_1_data));  // open: sel, clk, ld, clr
  RAM #(.addrWidth(10)) ram_2 (.addr(in_1[9:0]), .data(ram_2_data));  // open: sel, clk, ld, clr
  RAM #(.addrWidth(10)) ram_3 (.addr(in_1[9:0]), .data(ram_3_data));  // open: sel, clk, ld, clr
  RAM #(.addrWidth(10)) ram_4 (.addr(in_1[9:0]), .data(ram_4_data));  // open: sel, clk, ld, clr
  Multiplexer #(.select(2), .width(8), .enable("false")) multiplexer_1 (
    .in0(ram_1_data), .in1(ram_2_data), .in2(ram_3_data), .in3(ram_4_data), .out(out_2), .sel(in_1[11:10]));

  // Other names for the same wires on the sheet: bits_10_11[1:0] = in_1[11:10]
endmodule
