// Logisim project dictionary.circ as structural Verilog: 4 circuits, main circuit main
module main (
  input  [5:0] read_key,
  input  [7:0] write_value,
  input  [5:0] write_key,
  input  write_enable,
  output [7:0] read_value
);

  wire g1, g2, g3, g4, g5, g6, readreg_1_key_output, readreg_2_key_output, readreg_3_key_output,
       readreg_4_key_output, readreg_5_key_output, readreg_6_key_output, readreg_7_key_output,
       readreg_8_key_output, transistor_4_out, transistor_8_out, transistor_12_out, transistor_16_out,
       transistor_20_out, transistor_24_out, transistor_28_out;
  wire [6:0] generalreg_1_key_output, generalreg_2_key_output, generalreg_3_key_output,
       generalreg_4_key_output, generalreg_5_key_output, generalreg_6_key_output, generalreg_7_key_output,
       generalreg_8_key_output, transistor_3_out, transistor_7_out, transistor_11_out, transistor_15_out,
       transistor_19_out, transistor_23_out, transistor_27_out;
  wire [7:0] generalreg_1_value_output, generalreg_2_value_output, generalreg_3_value_output,
       generalreg_4_value_output, generalreg_5_value_output, generalreg_6_value_output,
       generalreg_7_value_output, generalreg_8_value_output, transistor_2_out, transistor_6_out,
       transistor_10_out, transistor_14_out, transistor_18_out, transistor_22_out, transistor_26_out;

  readReg readreg_1 (
    .read_key({1'b1, read_key}), .key_compare(generalreg_1_key_output), .key_output(readreg_1_key_output));
  generalReg generalreg_1 (
    .write_value(write_value), .write_key({1'b1, write_key}), .write_enable(write_enable),
    .value_output(generalreg_1_value_output), .key_output(generalreg_1_key_output));
  Transistor #(.\type ("n"), .gate("br"), .width(8)) transistor_1 (
    .in(write_value), .out(read_value), .gate(readreg_1_key_output));
  // Probe on generalreg_1_value_output
  // Probe on generalreg_1_key_output
  duplicatekey duplicatekey_1 (.read_key({1'b1, write_key}), .key_compare(generalreg_1_key_output), .write_enable(g1));
  Transistor #(.width(8)) transistor_2 (.in(generalreg_1_value_output), .out(transistor_2_out), .gate(g1));
  Transistor #(.width(7)) transistor_3 (.in(generalreg_1_key_output), .out(transistor_3_out), .gate(g1));
  Transistor transistor_4 (.in(write_enable), .out(transistor_4_out), .gate(g1));
  generalReg generalreg_2 (
    .write_value(transistor_2_out), .write_key(transistor_3_out), .write_enable(transistor_4_out),
    .value_output(generalreg_2_value_output), .key_output(generalreg_2_key_output));
  // Probe on generalreg_2_value_output
  // Probe on generalreg_2_key_output
  duplicatekey duplicatekey_2 (.read_key({1'b1, write_key}), .key_compare(generalreg_2_key_output), .write_enable(g2));
  Transistor #(.\type ("n"), .gate("br"), .width(8)) transistor_5 (
    .in(generalreg_2_value_output), .out(read_value), .gate(readreg_2_key_output));
  readReg readreg_2 (
    .read_key({1'b1, read_key}), .key_compare(generalreg_2_key_output), .key_output(readreg_2_key_output));
  Transistor #(.width(8)) transistor_6 (.in(generalreg_2_value_output), .out(transistor_6_out), .gate(g2));
  Transistor #(.width(7)) transistor_7 (.in(generalreg_2_key_output), .out(transistor_7_out), .gate(g2));
  Transistor transistor_8 (.in(write_enable), .out(transistor_8_out), .gate(g2));
  generalReg generalreg_3 (
    .write_value(transistor_6_out), .write_key(transistor_7_out), .write_enable(transistor_8_out),
    .value_output(generalreg_3_value_output), .key_output(generalreg_3_key_output));
  // Probe on generalreg_3_value_output
  duplicatekey duplicatekey_3 (.read_key({1'b1, write_key}), .key_compare(generalreg_3_key_output), .write_enable(g3));
  Transistor #(.\type ("n"), .gate("br"), .width(8)) transistor_9 (
    .in(generalreg_3_value_output), .out(read_value), .gate(readreg_3_key_output));
  readReg readreg_3 (
    .read_key({1'b1, read_key}), .key_compare(generalreg_3_key_output), .key_output(readreg_3_key_output));
  // Probe on generalreg_3_key_output
  Transistor #(.width(8)) transistor_10 (.in(generalreg_3_value_output), .out(transistor_10_out), .gate(g3));
  Transistor #(.width(7)) transistor_11 (.in(generalreg_3_key_output), .out(transistor_11_out), .gate(g3));
  Transistor transistor_12 (.in(write_enable), .out(transistor_12_out), .gate(g3));
  generalReg generalreg_4 (
    .write_value(transistor_10_out), .write_key(transistor_11_out), .write_enable(transistor_12_out),
    .value_output(generalreg_4_value_output), .key_output(generalreg_4_key_output));
  readReg readreg_4 (
    .read_key({1'b1, read_key}), .key_compare(generalreg_4_key_output), .key_output(readreg_4_key_output));
  // Probe on generalreg_4_value_output
  // Probe on generalreg_4_key_output
  duplicatekey duplicatekey_4 (.read_key({1'b1, write_key}), .key_compare(generalreg_4_key_output), .write_enable(g4));
  Transistor #(.\type ("n"), .gate("br"), .width(8)) transistor_13 (
    .in(generalreg_4_value_output), .out(read_value), .gate(readreg_4_key_output));
  Transistor #(.width(8)) transistor_14 (.in(generalreg_4_value_output), .out(transistor_14_out), .gate(g4));
  Transistor #(.width(7)) transistor_15 (.in(generalreg_4_key_output), .out(transistor_15_out), .gate(g4));
  generalReg generalreg_5 (
    .write_value(transistor_14_out), .write_key(transistor_15_out), .write_enable(transistor_16_out),
    .value_output(generalreg_5_value_output), .key_output(generalreg_5_key_output));
  Transistor transistor_16 (.in(write_enable), .out(transistor_16_out), .gate(g4));
  Transistor #(.\type ("n"), .gate("br"), .width(8)) transistor_17 (
    .in(generalreg_5_value_output), .out(read_value), .gate(readreg_5_key_output));
  readReg readreg_5 (
    .read_key({1'b1, read_key}), .key_compare(generalreg_5_key_output), .key_output(readreg_5_key_output));
  // Probe on generalreg_5_value_output
  // Probe on generalreg_5_key_output
  duplicatekey duplicatekey_5 (.read_key({1'b1, write_key}), .key_compare(generalreg_5_key_output), .write_enable(g5));
  Transistor #(.width(8)) transistor_18 (.in(generalreg_5_value_output), .out(transistor_18_out), .gate(g5));
  Transistor #(.width(7)) transistor_19 (.in(generalreg_5_key_output), .out(transistor_19_out), .gate(g5));
  Transistor transistor_20 (.in(write_enable), .out(transistor_20_out), .gate(g5));
  generalReg generalreg_6 (
    .write_value(transistor_18_out), .write_key(transistor_19_out), .write_enable(transistor_20_out),
    .value_output(generalreg_6_value_output), .key_output(generalreg_6_key_output));
  // Probe on generalreg_6_value_output
  Transistor #(.\type ("n"), .gate("br"), .width(8)) transistor_21 (
    .in(generalreg_6_value_output), .out(read_value), .gate(readreg_6_key_output));
  readReg readreg_6 (
    .read_key({1'b1, read_key}), .key_compare(generalreg_6_key_output), .key_output(readreg_6_key_output));
  // Probe on generalreg_6_key_output
  duplicatekey duplicatekey_6 (.read_key({1'b1, write_key}), .key_compare(generalreg_6_key_output), .write_enable(g6));
  Transistor #(.width(8)) transistor_22 (.in(generalreg_6_value_output), .out(transistor_22_out), .gate(g6));
  Transistor #(.width(7)) transistor_23 (.in(generalreg_6_key_output), .out(transistor_23_out), .gate(g6));
  Transistor transistor_24 (.in(write_enable), .out(transistor_24_out), .gate(g6));
  generalReg generalreg_7 (
    .write_value(transistor_22_out), .write_key(transistor_23_out), .write_enable(transistor_24_out),
    .value_output(generalreg_7_value_output), .key_output(generalreg_7_key_output));
  readReg readreg_7 (
    .read_key({1'b1, read_key}), .key_compare(generalreg_7_key_output), .key_output(readreg_7_key_output));
  // Probe on generalreg_7_value_output
  // Probe on generalreg_7_key_output
  Transistor #(.\type ("n"), .gate("br"), .width(8)) transistor_25 (
    .in(generalreg_7_value_output), .out(read_value), .gate(readreg_7_key_output));
  duplicatekey duplicatekey_7 (.read_key({1'b1, write_key}), .key_compare(generalreg_7_key_output), .write_enable(g6));
  Transistor #(.width(8)) transistor_26 (.in(generalreg_7_value_output), .out(transistor_26_out), .gate(g6));
  Transistor #(.width(7)) transistor_27 (.in(generalreg_7_key_output), .out(transistor_27_out), .gate(g6));
  Transistor transistor_28 (.in(write_enable), .out(transistor_28_out), .gate(g6));
  generalReg generalreg_8 (
    .write_value(transistor_26_out), .write_key(transistor_27_out), .write_enable(transistor_28_out),
    .value_output(generalreg_8_value_output), .key_output(generalreg_8_key_output));
  // Probe on {1'b1, write_key}
  readReg readreg_8 (
    .read_key({1'b1, read_key}), .key_compare(generalreg_8_key_output), .key_output(readreg_8_key_output));
  Transistor #(.\type ("n"), .gate("br"), .width(8)) transistor_29 (
    .in(generalreg_8_value_output), .out(read_value), .gate(readreg_8_key_output));

  // Other names for the same wires on the sheet: rk[5:0] = read_key; rv[7:0] = read_value
endmodule

module generalReg (
  input  [7:0] write_value,
  input  [6:0] write_key,
  input  write_enable,
  output [7:0] value_output,
  output [6:0] key_output
);

  Register #(.width(7)) register_1 (.D(write_key), .Q(key_output), .clk(write_enable));  // open: en, clr
  Register register_2 (.D(write_value), .Q(value_output), .clk(write_enable));  // open: en, clr
endmodule

module readReg (
  input  [6:0] read_key,
  input  [6:0] key_compare,
  output key_output
);

  wire xnor_1_out, xnor_2_out, xnor_3_out, xnor_4_out, xnor_5_out, xnor_6_out, xnor_7_out;

  xnor xnor_1 (xnor_1_out, read_key[0], key_compare[0]);
  xnor xnor_2 (xnor_2_out, read_key[1], key_compare[1]);
  xnor xnor_3 (xnor_3_out, read_key[2], key_compare[2]);
  xnor xnor_4 (xnor_4_out, read_key[3], key_compare[3]);
  xnor xnor_5 (xnor_5_out, read_key[4], key_compare[4]);
  xnor xnor_6 (xnor_6_out, read_key[5], key_compare[5]);
  xnor xnor_7 (xnor_7_out, read_key[6], key_compare[6]);
  and and_1 (key_output, xnor_1_out, xnor_2_out, xnor_3_out, xnor_7_out, xnor_4_out, xnor_5_out, xnor_6_out);
endmodule

module duplicatekey (
  input  [6:0] read_key,
  input  [6:0] key_compare,
  output write_enable
);

  readReg readreg_1 (.read_key(read_key), .key_compare(key_compare), .key_output(write_enable));
endmodule
