// Logisim project binary-coded-decimal.circ as structural Verilog: 2 circuits, main circuit main
module main (
  input  [7:0] in_1,
  input  [7:0] in_2,
  output [8:0] out_3
);

  add add_1 (
    .input_a(in_1), .input_b(in_2), .hundreds_output(out_3[8]), .ones_output(out_3[3:0]),
    .tens_output(out_3[7:4]));
endmodule

module add (
  input  [7:0] input_a,
  input  [7:0] input_b,
  output [3:0] ones_output,
  output [3:0] tens_output,
  output hundreds_output
);

  wire adder_2_cout, comparator_2_gt;
  wire [3:0] adder_1_out, adder_2_out, subtractor_1_out, subtractor_2_out;

  Adder #(.width(4)) adder_1 (
    .a(input_a[7:4]), .b(input_b[7:4]), .out(adder_1_out), .cin(comparator_2_gt));  // open: cout
  Adder #(.width(4)) adder_2 (.a(input_a[3:0]), .b(input_b[3:0]), .out(adder_2_out), .cout(adder_2_cout));  // open: cin
  Comparator #(.width(4), .mode("unsigned")) comparator_1 (
    .a(adder_1_out), .b(4'b1001), .gt(hundreds_output));  // open: eq, lt
  Comparator #(.width(4), .mode("unsigned")) comparator_2 (
    .a(adder_2_out), .b(4'b1001), .gt(comparator_2_gt));  // open: eq, lt
  Multiplexer #(.width(4)) multiplexer_1 (
    .in0(adder_1_out), .in1(subtractor_1_out), .out(tens_output), .sel(hundreds_output));  // open: en
  Multiplexer #(.width(4)) multiplexer_2 (
    .in0(adder_2_out), .in1(subtractor_2_out), .out(ones_output), .sel(comparator_2_gt));  // open: en
  // Probe on adder_2_out
  // Probe on adder_1_out
  Subtractor #(.width(4)) subtractor_1 (.a(adder_1_out), .b(4'b1010), .out(subtractor_1_out));  // open: bin, bout
  Subtractor #(.width(4)) subtractor_2 (.a(adder_2_out), .b(4'b1010), .out(subtractor_2_out));  // open: bin, bout
  // Probe on subtractor_1_out
  // Probe on subtractor_2_out
endmodule
