// Logisim project arm-processor.circ as structural Verilog: 4 circuits, main circuit main
module main (
  input  [31:0] operand,
  input  [3:0] operation,
  input  Id_cc,
  input  [31:0] operand_0,
  input  [2:0] Rn,
  input  [31:0] operand_1,
  input  [2:0] Rd,
  input  [31:0] Rd_val,
  input  clk,
  input  [2:0] Rm,
  output N,
  output Z,
  output P,
  output [31:0] result,
  output [31:0] Rn_val,
  output [31:0] Rm_val
);

  // register_file register_file_1: pin names not known; wires that end beside it: Rd, Rd_val, clk, Rn, Rn_val, Rm_val, Rm
  condition_code_register CCR (.operand(operand), .Id_cc(Id_cc), .N(N), .Z(Z), .P(P));
  ALU alu_1 (.operation(operation), .operand_0(operand_0), .operand_1(operand_1), .result(result));
endmodule

module condition_code_register (
  input  [31:0] operand,
  input  Id_cc,
  output N,
  output Z,
  output P
);

  wire and_1_out, comparator_1_eq, not_1_out, not_2_out;

  not not_1 (not_1_out, operand[31]);
  Comparator #(.width(32)) comparator_1 (.a({32{1'b0}}), .b(operand), .eq(comparator_1_eq));  // open: gt, lt
  Register #(.width(1)) register_1 (.D(operand[31]), .Q(N), .clk(Id_cc));  // open: en, clr
  not not_2 (not_2_out, comparator_1_eq);
  Register #(.width(1)) register_2 (.D(comparator_1_eq), .Q(Z), .clk(Id_cc));  // open: en, clr
  and and_1 (and_1_out, not_2_out, not_1_out);
  Register #(.width(1)) register_3 (.D(and_1_out), .Q(P), .clk(Id_cc));  // open: en, clr
endmodule

module ALU (
  input  [3:0] operation,
  input  [31:0] operand_0,
  input  [31:0] operand_1,
  output [31:0] result
);

  wire [31:0] adder_1_out, and_1_out, not_1_out, or_1_out, subtractor_1_out, subtractor_2_out, xor_1_out;

  assign not_1_out = ~operand_1;  // NOT_Gate not_1, 32 bits wide
  assign and_1_out = operand_0 & operand_1;  // AND_Gate and_1, 32 bits wide
  assign xor_1_out = operand_0 ^ operand_1;  // XOR_Gate xor_1, 32 bits wide
  Subtractor #(.width(32)) subtractor_1 (.a(operand_0), .b(operand_1), .out(subtractor_1_out));  // open: bin, bout
  Subtractor #(.width(32)) subtractor_2 (.a(operand_1), .b(operand_0), .out(subtractor_2_out));  // open: bin, bout
  Adder #(.width(32)) adder_1 (.a(operand_0), .b(operand_1), .out(adder_1_out));  // open: cin, cout
  assign or_1_out = operand_0 | operand_1;  // OR_Gate or_1, 32 bits wide
  Multiplexer #(.select(4), .width(32)) multiplexer_1 (
    .in0(and_1_out), .in1(xor_1_out), .in2(subtractor_1_out), .in3(subtractor_2_out), .in4(adder_1_out),
    .in12(or_1_out), .in13(operand_1), .in15(not_1_out), .out(result), .sel(operation));  // open: in5, in6, in7, in8, in9, in10, in11, in14, en
endmodule

// RF
module register_file (
  input  [2:0] Rn,
  input  [31:0] Rd_val,
  input  [2:0] Rd,
  input  [2:0] Rm,
  input  clk,
  output [31:0] Rn_val,
  output [31:0] Rm_val
);

  wire decoder_1_out0, decoder_1_out1, decoder_1_out2, decoder_1_out3, decoder_1_out4, decoder_1_out5,
       decoder_1_out6, decoder_1_out7;
  wire [31:0] register_1_q, register_2_q, register_3_q, register_4_q, register_5_q, register_6_q,
       register_7_q, register_8_q;

  Decoder #(.select(3)) decoder_1 (
    .out0(decoder_1_out0), .out1(decoder_1_out1), .out2(decoder_1_out2), .out3(decoder_1_out3),
    .out4(decoder_1_out4), .out5(decoder_1_out5), .out6(decoder_1_out6), .out7(decoder_1_out7), .sel(Rd));  // open: en
  Register #(.width(32)) register_1 (.D(Rd_val), .en(decoder_1_out0), .Q(register_1_q), .clk(clk));  // open: clr
  Register #(.width(32)) register_2 (.D(Rd_val), .en(decoder_1_out1), .Q(register_2_q), .clk(clk));  // open: clr
  Register #(.width(32)) register_3 (.D(Rd_val), .en(decoder_1_out2), .Q(register_3_q), .clk(clk));  // open: clr
  Register #(.width(32)) register_4 (.D(Rd_val), .en(decoder_1_out3), .Q(register_4_q), .clk(clk));  // open: clr
  Register #(.width(32)) register_5 (.D(Rd_val), .en(decoder_1_out4), .Q(register_5_q), .clk(clk));  // open: clr
  Register #(.width(32)) register_6 (.D(Rd_val), .en(decoder_1_out5), .Q(register_6_q), .clk(clk));  // open: clr
  Register #(.width(32)) register_7 (.D(Rd_val), .en(decoder_1_out6), .Q(register_7_q), .clk(clk));  // open: clr
  Register #(.width(32)) register_8 (.D(Rd_val), .en(decoder_1_out7), .Q(register_8_q), .clk(clk));  // open: clr
  Multiplexer #(.select(3), .width(32)) multiplexer_1 (
    .in0(register_1_q), .in1(register_2_q), .in2(register_3_q), .in3(register_4_q), .in4(register_5_q),
    .in5(register_6_q), .in6(register_7_q), .in7(register_8_q), .out(Rn_val), .sel(Rn));  // open: en
  Multiplexer #(.select(3), .width(32)) multiplexer_2 (
    .in0(register_1_q), .in1(register_2_q), .in2(register_3_q), .in3(register_4_q), .in4(register_5_q),
    .in5(register_6_q), .in6(register_7_q), .in7(register_8_q), .out(Rm_val), .sel(Rm));  // open: en
endmodule
