// Logisim project hw05.circ as structural Verilog: 5 circuits, main circuit main
module main (
  input  [31:0] instructions,
  input  load,
  input  clock,
  input  enable
);

  wire and_1_out, branch, is_and_out, is_bool, is_eor_out, is_orr_out, multiplexer_1_out, not_1_out,
       not_2_out, not_3_out, or_2_out, or_3_out;
  wire [7:0] adder_1_out, counter_1_q;
  wire [31:0] bit_extender_1_out, bit_extender_2_out, multiplexer_2_out, multiplexer_3_out,
       register_file_1_rm_val, register_file_1_rn_val, result;

  branch branch_1 (.cond(instructions[31:28]), .clock(clock), .D(result), .id_cc(instructions[20]), .branch(branch));
  and is_eor (is_eor_out, instructions[21], ~instructions[22], ~instructions[23], ~instructions[24]);  // AND_Gate
  and is_and (is_and_out, ~instructions[21], ~instructions[22], ~instructions[23], ~instructions[24]);  // AND_Gate
  or or_1 (is_bool, is_and_out, is_eor_out, is_orr_out);
  and is_orr (is_orr_out, ~instructions[21], ~instructions[22], instructions[23], instructions[24]);  // AND_Gate
  and and_1 (and_1_out, branch, instructions[27]);
  or or_2 (or_2_out, branch, instructions[27]);
  not not_1 (not_1_out, instructions[27]);
  Adder adder_1 (.a(instructions[7:0]), .b(counter_1_q), .out(adder_1_out));  // open: cin, cout
  Counter #(.trigger("falling")) counter_1 (
    .load(and_1_out), .D(adder_1_out), .count(not_1_out), .Q(counter_1_q), .clk(or_2_out));  // open: carry, clr
  Multiplexer multiplexer_1 (.in0(clock), .in1(1'b0), .out(multiplexer_1_out), .sel(or_3_out));  // open: en
  or or_3 (or_3_out, instructions[27], instructions[20]);
  not not_2 (not_2_out, multiplexer_1_out);
  RAM #(.dataWidth(32)) ram_1 (
    .addr(counter_1_q), .data(instructions), .clk(not_2_out), .ld(not_3_out));  // open: sel, clr
  not not_3 (not_3_out, load);
  // Probe on instructions[15:12]
  assign bit_extender_1_out = {{20{1'b0}}, instructions[11:0]};  // Bit_Extender bit_extender_1
  register_file register_file_1 (
    .en(enable), .Rd_val(result), .clk(multiplexer_1_out), .Rd(instructions[15:12]),
    .Rn(instructions[19:16]), .Rm(instructions[3:0]), .Rn_val(register_file_1_rn_val),
    .Rm_val(register_file_1_rm_val));
  // Probe on instructions[24:21]
  ALU alu_1 (
    .operand_0(register_file_1_rn_val), .operand_1(multiplexer_2_out), .operation(instructions[24:21]),
    .result(result));
  // Probe on register_file_1_rn_val
  Multiplexer #(.width(32), .enable("false")) multiplexer_2 (
    .in0(register_file_1_rm_val), .in1(multiplexer_3_out), .out(multiplexer_2_out), .sel(instructions[25]));
  Multiplexer #(.width(32), .enable("false")) multiplexer_3 (
    .in0(bit_extender_2_out), .in1(bit_extender_1_out), .out(multiplexer_3_out), .sel(is_bool));
  assign bit_extender_2_out = {{20{instructions[11]}}, instructions[11:0]};  // Bit_Extender bit_extender_2
  // Probe on result
  // Probe on multiplexer_2_out

  // Other names for the same wires on the sheet: imm12[11:0] = instructions[11:0]; instruction[31:0] = instructions;
  //   offset[7:0] = instructions[7:0]; Rm[3:0] = instructions[3:0]; Rd[3:0] = instructions[15:12];
  //   Rn[3:0] = instructions[19:16]; compare = instructions[20]; opcode[3:0] = instructions[24:21];
  //   is_imm = instructions[25]; a_branch = instructions[27]; cond[3:0] = instructions[31:28]
endmodule

// RF
module register_file (
  input  en,
  input  [31:0] Rd_val,
  input  clk,
  input  [3:0] Rd,
  input  [3:0] Rn,
  input  [3:0] Rm,
  output [31:0] Rn_val,
  output [31:0] Rm_val
);

  wire decoder_1_out0, decoder_1_out1, decoder_1_out2, decoder_1_out3, decoder_1_out4, decoder_1_out5,
       decoder_1_out6, decoder_1_out7;
  wire [31:0] register_1_q, register_2_q, register_3_q, register_4_q, register_5_q, register_6_q,
       register_7_q, register_8_q;

  Decoder #(.select(3), .disabled(0)) decoder_1 (
    .out0(decoder_1_out0), .out1(decoder_1_out1), .out2(decoder_1_out2), .out3(decoder_1_out3),
    .out4(decoder_1_out4), .out5(decoder_1_out5), .out6(decoder_1_out6), .out7(decoder_1_out7),
    .sel(Rd[2:0]), .en(clk));
  Register #(.width(32)) register_1 (.D(Rd_val), .en(en), .Q(register_1_q), .clk(decoder_1_out7));  // open: clr
  Register #(.width(32)) register_2 (.D(Rd_val), .en(en), .Q(register_2_q), .clk(decoder_1_out6));  // open: clr
  Register #(.width(32)) register_3 (.D(Rd_val), .en(en), .Q(register_3_q), .clk(decoder_1_out5));  // open: clr
  Register #(.width(32)) register_4 (.D(Rd_val), .en(en), .Q(register_4_q), .clk(decoder_1_out4));  // open: clr
  Register #(.width(32)) register_5 (.D(Rd_val), .en(en), .Q(register_5_q), .clk(decoder_1_out3));  // open: clr
  Register #(.width(32)) register_6 (.D(Rd_val), .en(en), .Q(register_6_q), .clk(decoder_1_out2));  // open: clr
  Register #(.width(32)) register_7 (.D(Rd_val), .en(en), .Q(register_7_q), .clk(decoder_1_out1));  // open: clr
  Register #(.width(32)) register_8 (.D(Rd_val), .en(en), .Q(register_8_q), .clk(decoder_1_out0));  // open: clr
  Multiplexer #(.select(3), .width(32)) multiplexer_1 (
    .in0(register_8_q), .in1(register_7_q), .in2(register_6_q), .in3(register_5_q), .in4(register_4_q),
    .in5(register_3_q), .in6(register_2_q), .in7(register_1_q), .out(Rn_val), .sel(Rn[2:0]));  // open: en
  Multiplexer #(.select(3), .width(32)) multiplexer_2 (
    .in0(register_8_q), .in1(register_7_q), .in2(register_6_q), .in3(register_5_q), .in4(register_4_q),
    .in5(register_3_q), .in6(register_2_q), .in7(register_1_q), .out(Rm_val), .sel(Rm[2:0]));  // open: en
endmodule

module ALU (
  input  [31:0] operand_0,
  input  [31:0] operand_1,
  input  [3:0] operation,
  output [31:0] result
);

  wire [31:0] adder_1_out, and_1_out, not_1_out, or_1_out, subtractor_1_out, subtractor_2_out, xor_1_out;

  assign and_1_out = operand_0 & operand_1;  // AND_Gate and_1, 32 bits wide
  assign xor_1_out = operand_0 ^ operand_1;  // XOR_Gate xor_1, 32 bits wide
  Subtractor #(.width(32)) subtractor_1 (.a(operand_0), .b(operand_1), .out(subtractor_1_out));  // open: bin, bout
  Subtractor #(.width(32)) subtractor_2 (.a(operand_1), .b(operand_0), .out(subtractor_2_out));  // open: bin, bout
  Adder #(.width(32)) adder_1 (.a(operand_0), .b(operand_1), .out(adder_1_out));  // open: cin, cout
  assign or_1_out = operand_0 | operand_1;  // OR_Gate or_1, 32 bits wide
  assign not_1_out = ~operand_1;  // NOT_Gate not_1, 32 bits wide
  Multiplexer #(.select(4), .width(32), .enable("false")) multiplexer_1 (
    .in0(and_1_out), .in1(xor_1_out), .in2(subtractor_1_out), .in3(subtractor_2_out), .in4(adder_1_out),
    .in10(subtractor_1_out), .in12(or_1_out), .in13(operand_1), .in15(not_1_out), .out(result),
    .sel(operation));  // open: in5, in6, in7, in8, in9, in11, in14
endmodule

// CCR
module condition_code_register (
  input  [31:0] D,
  input  clk,
  input  en,
  output Z,
  output P,
  output N
);

  wire and_1_out, and_2_out;

  and and_1 (and_1_out, ~D[0], ~D[1], ~D[2], ~D[3], ~D[4], ~D[5], ~D[6], ~D[7], ~D[8], ~D[9], ~D[10], ~D[11], ~D[12], ~D[13], ~D[14], ~D[15], ~D[16], ~D[17], ~D[18], ~D[19], ~D[20], ~D[21], ~D[22], ~D[23], ~D[24], ~D[25], ~D[26], ~D[27], ~D[28], ~D[29], ~D[30], ~D[31]);  // AND_Gate
  and and_2 (and_2_out, ~and_1_out, ~D[31]);  // AND_Gate
  Register #(.width(1)) register_1 (.D(and_1_out), .en(en), .Q(Z), .clk(clk));  // open: clr
  Register #(.width(1)) register_2 (.D(and_2_out), .en(en), .Q(P), .clk(clk));  // open: clr
  Register #(.width(1)) register_3 (.D(D[31]), .en(en), .Q(N), .clk(clk));  // open: clr
endmodule

// B
module branch (
  input  [3:0] cond,
  input  [31:0] D,
  input  clock,
  input  id_cc,
  output branch
);

  wire condition_code_register_1_n, condition_code_register_1_p, condition_code_register_1_z, not_1_out,
       or_1_out, or_2_out;

  condition_code_register condition_code_register_1 (
    .D(D), .clk(clock), .en(id_cc), .Z(condition_code_register_1_z), .P(condition_code_register_1_p),
    .N(condition_code_register_1_n));
  or or_1 (or_1_out, condition_code_register_1_z, condition_code_register_1_p);
  or or_2 (or_2_out, condition_code_register_1_z, condition_code_register_1_n);
  not not_1 (not_1_out, condition_code_register_1_z);
  Multiplexer #(.select(4)) multiplexer_1 (
    .in0(condition_code_register_1_z), .in1(not_1_out), .in10(or_1_out), .in11(condition_code_register_1_n),
    .in12(condition_code_register_1_p), .in13(or_2_out), .in14(1'b1), .out(branch), .sel(cond));  // open: in2, in3, in4, in5, in6, in7, in8, in9, in15, en
endmodule
