// Logisim project single-instruction-cpu.circ as structural Verilog: 5 circuits, main circuit main
module main (
  input  clock,
  input  [31:0] ARM32
);

  CPU cpu_1 (.in_1(clock), .arm_instruction(ARM32));
endmodule

module ALU (
  input  [3:0] operation,
  input  [31:0] rn_val,
  input  [31:0] rm_val,
  output [31:0] result
);

  wire [31:0] adder_1_out, and_1_out, not_1_out, or_1_out, subtractor_1_out, subtractor_2_out, xor_1_out;

  assign and_1_out = rn_val & rm_val;  // AND_Gate and_1, 32 bits wide
  assign xor_1_out = rn_val ^ rm_val;  // XOR_Gate xor_1, 32 bits wide
  Subtractor #(.width(32)) subtractor_1 (.a(rn_val), .b(rm_val), .out(subtractor_1_out));  // open: bin, bout
  Subtractor #(.width(32)) subtractor_2 (.a(rm_val), .b(rn_val), .out(subtractor_2_out));  // open: bin, bout
  Adder #(.width(32)) adder_1 (.a(rn_val), .b(rm_val), .out(adder_1_out));  // open: cin, cout
  assign or_1_out = rn_val | rm_val;  // OR_Gate or_1, 32 bits wide
  assign not_1_out = ~rm_val;  // NOT_Gate not_1, 32 bits wide
  Multiplexer #(.select(4), .width(32)) multiplexer_1 (
    .in0(and_1_out), .in1(xor_1_out), .in2(subtractor_1_out), .in3(subtractor_2_out), .in4(adder_1_out),
    .in12(or_1_out), .in13(rm_val), .in15(not_1_out), .out(result), .sel(operation));  // open: in5, in6, in7, in8, in9, in10, in11, in14, en
endmodule

// RF
module register_file (
  input  [3:0] Rn,
  input  [31:0] Rd_val,
  input  [3:0] Rd,
  input  [3:0] Rm,
  input  clk,
  output [31:0] Rn_val,
  output [31:0] Rm_val
);

  wire decoder_1_out0, decoder_1_out1, decoder_1_out2, decoder_1_out3, decoder_1_out4, decoder_1_out5,
       decoder_1_out6, decoder_1_out7;
  wire [31:0] register_1_q, register_2_q, register_3_q, register_4_q, register_5_q, register_6_q,
       register_7_q, register_8_q;

  Decoder #(.select(4)) decoder_1 (
    .out0(decoder_1_out0), .out1(decoder_1_out1), .out2(decoder_1_out2), .out3(decoder_1_out3),
    .out4(decoder_1_out4), .out5(decoder_1_out5), .out6(decoder_1_out6), .out7(decoder_1_out7), .sel(Rd));  // open: out8, out9, out10, out11, out12, out13, out14, out15, en
  Register #(.width(32)) register_1 (.D(Rd_val), .en(decoder_1_out0), .Q(register_1_q), .clk(clk));  // open: clr
  Register #(.width(32)) register_2 (.D(Rd_val), .en(decoder_1_out1), .Q(register_2_q), .clk(clk));  // open: clr
  Register #(.width(32)) register_3 (.D(Rd_val), .en(decoder_1_out2), .Q(register_3_q), .clk(clk));  // open: clr
  Register #(.width(32)) register_4 (.D(Rd_val), .en(decoder_1_out3), .Q(register_4_q), .clk(clk));  // open: clr
  Register #(.width(32)) register_5 (.D(Rd_val), .en(decoder_1_out4), .Q(register_5_q), .clk(clk));  // open: clr
  Register #(.width(32)) register_6 (.D(Rd_val), .en(decoder_1_out5), .Q(register_6_q), .clk(clk));  // open: clr
  Register #(.width(32)) register_7 (.D(Rd_val), .en(decoder_1_out6), .Q(register_7_q), .clk(clk));  // open: clr
  Register #(.width(32)) register_8 (.D(Rd_val), .en(decoder_1_out7), .Q(register_8_q), .clk(clk));  // open: clr
  Multiplexer #(.select(4), .width(32)) multiplexer_1 (
    .in0(register_1_q), .in1(register_2_q), .in2(register_3_q), .in3(register_4_q), .in4(register_5_q),
    .in5(register_6_q), .in6(register_7_q), .in7(register_8_q), .out(Rn_val), .sel(Rn));  // open: in8, in9, in10, in11, in12, in13, in14, in15, en
  Multiplexer #(.select(4), .width(32)) multiplexer_2 (
    .in0(register_1_q), .in1(register_2_q), .in2(register_3_q), .in3(register_4_q), .in4(register_5_q),
    .in5(register_6_q), .in6(register_7_q), .in7(register_8_q), .out(Rm_val), .sel(Rm));  // open: in8, in9, in10, in11, in12, in13, in14, in15, en
endmodule

// OT
module operation_translator (
  input  [31:0] arm_instruction,
  output [3:0] rm,
  output [3:0] rd,
  output [11:0] imm12,
  output [3:0] rn,
  output [6:0] operation
);

  wire [11:4] demultiplexer_1_out0;

  // Probe on arm_instruction[11:0]
  Demultiplexer #(.width(12)) demultiplexer_1 (
    .out0({demultiplexer_1_out0, rm}), .out1(imm12), .in(arm_instruction[11:0]), .sel(arm_instruction[25]));  // open: en
  // Probe on imm12

  assign operation = arm_instruction[27:21];
  assign rd = arm_instruction[15:12];
  assign rn = arm_instruction[19:16];
endmodule

module CPU (
  input  in_1,
  input  [31:0] arm_instruction
);

  wire [3:0] operation_translator_1_rd, operation_translator_1_rm, operation_translator_1_rn;
  wire [6:0] operation_translator_1_operation;
  wire [31:0] alu_1_result, register_file_1_rm_val, register_file_1_rn_val;

  operation_translator operation_translator_1 (
    .arm_instruction(arm_instruction), .rm(operation_translator_1_rm), .rd(operation_translator_1_rd),
    .rn(operation_translator_1_rn), .operation(operation_translator_1_operation));  // open: imm12
  register_file register_file_1 (
    .Rd_val(alu_1_result), .clk(in_1), .Rd(operation_translator_1_rd), .Rn(operation_translator_1_rn),
    .Rn_val(register_file_1_rn_val), .Rm_val(register_file_1_rm_val), .Rm(operation_translator_1_rm));
  ALU alu_1 (
    .operation(operation_translator_1_operation[3:0]), .rn_val(register_file_1_rn_val),
    .rm_val(register_file_1_rm_val), .result(alu_1_result));
endmodule
