// Logisim project register-file.circ as structural Verilog: 1 circuit, main circuit main
module main (
  input  [2:0] Rd,
  input  [31:0] Rd_val,
  input  [2:0] Rn,
  input  [2:0] Rm,
  input  clk,
  output [31:0] Rn_val,
  output [31:0] Rm_val
);
endmodule
