// Logisim project traffic-light.circ as structural Verilog: 5 circuits, main circuit main
module main (
);

  wire light_1_green, light_1_red, light_1_yellow, light_2_green, light_2_red, light_2_yellow, reset_out,
       tick_out;
  wire [2:0] counter_1_q;
  wire [11:0] multiplexer_1_out;

  Button tick (.out(tick_out));
  Button reset (.out(reset_out));
  Counter #(.width(3), .max('h5)) counter_1 (
    .Q(counter_1_q), .clk(tick_out), .clr(reset_out));  // open: load, D, count, carry
  // Probe on counter_1_q
  Multiplexer #(.select(3), .width(12), .enable("false")) multiplexer_1 (
    .in0(12'ha69), .in1(12'h12), .in2(12'h24), .in3(12'h9), .in4(12'h480), .in5(12'h900),
    .out(multiplexer_1_out), .sel(counter_1_q));  // open: in6, in7
  light light_1 (
    .R_on(multiplexer_1_out[0]), .R_off(multiplexer_1_out[1]), .Y_on(multiplexer_1_out[2]),
    .Y_off(multiplexer_1_out[3]), .G_on(multiplexer_1_out[4]), .G_off(multiplexer_1_out[5]),
    .Red(light_1_red), .Yellow(light_1_yellow), .Green(light_1_green));
  LED led_1 (.in(light_1_red));
  LED led_2 (.in(light_1_yellow));
  LED led_3 (.in(light_1_green));
  light light_2 (
    .R_on(multiplexer_1_out[6]), .R_off(multiplexer_1_out[7]), .Y_on(multiplexer_1_out[8]),
    .Y_off(multiplexer_1_out[9]), .G_on(multiplexer_1_out[10]), .G_off(multiplexer_1_out[11]),
    .Red(light_2_red), .Yellow(light_2_yellow), .Green(light_2_green));
  LED led_4 (.in(light_2_red));
  LED led_5 (.in(light_2_yellow));
  LED led_6 (.in(light_2_green));

  // Notes on the sheet:
  //   North/South
  //   East/West
endmodule

module light (
  input  R_on,
  input  R_off,
  input  Y_on,
  input  Y_off,
  input  G_on,
  input  G_off,
  output Red,
  output Yellow,
  output Green
);

  D_Flip_Flop d_ff_1 (.Q(Red), .preset(R_on), .reset(R_off));  // open: clk, D, Qn, en
  D_Flip_Flop d_ff_2 (.Q(Yellow), .preset(Y_on), .reset(Y_off));  // open: clk, D, Qn, en
  D_Flip_Flop d_ff_3 (.Q(Green), .preset(G_on), .reset(G_off));  // open: clk, D, Qn, en
endmodule

module light_demo (
);

  wire button_1_out, button_2_out, button_3_out, button_4_out, button_5_out, button_6_out, light_1_green,
       light_1_red, light_1_yellow;

  Button button_1 (.out(button_1_out));
  Button button_2 (.out(button_2_out));
  Button button_3 (.out(button_3_out));
  Button button_4 (.out(button_4_out));
  Button button_5 (.out(button_5_out));
  Button button_6 (.out(button_6_out));
  LED led_1 (.in(light_1_red));
  light light_1 (
    .R_on(button_1_out), .R_off(button_2_out), .Y_on(button_3_out), .Y_off(button_4_out),
    .G_on(button_5_out), .G_off(button_6_out), .Red(light_1_red), .Yellow(light_1_yellow),
    .Green(light_1_green));
  LED led_2 (.in(light_1_yellow));
  LED led_3 (.in(light_1_green));
endmodule

module rom (
);

  wire light_1_green, light_1_red, light_1_yellow, light_2_green, light_2_red, light_2_yellow, reset_out,
       tick_out;
  wire [2:0] counter_1_q;
  wire [11:0] rom_1_data;

  Counter #(.width(3), .max('h5)) counter_1 (
    .Q(counter_1_q), .clk(tick_out), .clr(reset_out));  // open: load, D, count, carry
  Button tick (.out(tick_out));
  Button reset (.out(reset_out));
  ROM #(.addrWidth(3), .dataWidth(12)) rom_1 (.addr(counter_1_q), .data(rom_1_data));  // open: sel
  // Probe on counter_1_q
  LED led_1 (.in(light_1_red));
  light light_1 (
    .R_on(rom_1_data[0]), .R_off(rom_1_data[1]), .Y_on(rom_1_data[2]), .Y_off(rom_1_data[3]),
    .G_on(rom_1_data[4]), .G_off(rom_1_data[5]), .Red(light_1_red), .Yellow(light_1_yellow),
    .Green(light_1_green));
  LED led_2 (.in(light_1_yellow));
  LED led_3 (.in(light_1_green));
  LED led_4 (.in(light_2_red));
  light light_2 (
    .R_on(rom_1_data[6]), .R_off(rom_1_data[7]), .Y_on(rom_1_data[8]), .Y_off(rom_1_data[9]),
    .G_on(rom_1_data[10]), .G_off(rom_1_data[11]), .Red(light_2_red), .Yellow(light_2_yellow),
    .Green(light_2_green));
  LED led_5 (.in(light_2_yellow));
  LED led_6 (.in(light_2_green));

  // Notes on the sheet:
  //   contents of rom_1 (hex, n*v repeats v):
  //   a69 12 24 9 480 900
  //   North/South
  //   East/West
endmodule

module intermediate (
);

  wire light_1_green, light_1_red, light_1_yellow, light_2_green, light_2_red, light_2_yellow;
  wire [11:0] undriven;

  light light_1 (
    .R_on(undriven[0]), .R_off(undriven[1]), .Y_on(undriven[2]), .Y_off(undriven[3]), .G_on(undriven[4]),
    .G_off(undriven[5]), .Red(light_1_red), .Yellow(light_1_yellow), .Green(light_1_green));
  LED led_1 (.in(light_1_red));
  LED led_2 (.in(light_1_yellow));
  LED led_3 (.in(light_1_green));
  light light_2 (
    .R_on(undriven[6]), .R_off(undriven[7]), .Y_on(undriven[8]), .Y_off(undriven[9]), .G_on(undriven[10]),
    .G_off(undriven[11]), .Red(light_2_red), .Yellow(light_2_yellow), .Green(light_2_green));
  LED led_4 (.in(light_2_red));
  LED led_5 (.in(light_2_yellow));
  LED led_6 (.in(light_2_green));

  // Notes on the sheet:
  //   North/South
  //   East/West
endmodule
